# Fritzing sketch emetteurDHT11 (saved by Fritzing 0.9.2b)
circuit board: 10cm x 6cm
breadboards: 1

parts:
  Arduino = Arduino Nano (Rev3.0)
  RHT1 = Humidity and Temperature Sensor RHT03 [part_number=DTH11]
  U2 = RF-LINK_TX [part_number="XY-FST FS1000A" package=rf-link_tx]

nets:
  GND: Arduino.GND, RHT1.GND_2, U2.GND
  N1: Arduino.D5, RHT1.Data-signal
  N2: Arduino.D12/MISO, U2.DATA
  5V: Arduino.5V, RHT1.Vcc
  3V3: Arduino.3V3, U2.+5V

// code stored in the sketch: emDHT11.ino
// Partie radio
#include <VirtualWire.h>
int absdegres = 0;
int negatif = 2;
int humidite = 0;
int chaine = 0;
int led = 13;
char Message[VW_MAX_MESSAGE_LEN]; 

// Partie m?t?o
#include <dht.h>
dht DHT;
#define DHT11_PIN 5

void setup() {
  pinMode(led, OUTPUT);     
  vw_setup(2000); // bits de transmission par seconde
}

void loop() {
  int chk = DHT.read11(DHT11_PIN); // propriété ET méthode !
  absdegres = DHT.temperature;
  if(absdegres < 0) {
    absdegres = abs(DHT.temperature);
    negatif = 1;
  } else {
    absdegres = DHT.temperature;
    negatif = 2;
  }
  if(absdegres > 99) {absdegres = 99;}
  humidite = DHT.humidity;
  if(humidite < 0)  {humidite = 0;}
  if(humidite > 99) {humidite = 99;}
  // Valeurs
  chaine = negatif*10000 + absdegres*100 + humidite;
  // Conversion du int en tableau de chars 
  itoa(chaine,Message,10);  // 10 car d?cimal
  // S?quence de transmission
  digitalWrite(led, HIGH);
  vw_send((uint8_t *)Message, strlen(Message));
  vw_wait_tx(); // On attend la fin de la transmission
  digitalWrite(led, LOW);
  delay(2000);  // et on se repose un peu...
}

// code stored in the sketch: emetteurDHT11.ino
// Partie radio
#include <VirtualWire.h>
int absdegres = 0;
int negatif = 2;
int humidite = 0;
int chaine = 0;
int led = 13;
char Message[VW_MAX_MESSAGE_LEN]; 

// Partie météo
#include <dht.h>
dht DHT;
#define DHT11_PIN 5

void setup() {
  pinMode(led, OUTPUT);     
  vw_setup(2000); // bits de transmission par seconde
}

void loop() {
  int chk = DHT.read11(DHT11_PIN); // propriété ET méthode !
  absdegres = DHT.temperature;
  if(absdegres < 0) {
    absdegres = abs(DHT.temperature);
    negatif = 1;
  } else {
    absdegres = DHT.temperature;
    negatif = 2;
  }
  if(absdegres > 99) {absdegres = 99;}
  humidite = DHT.humidity;
  if(humidite < 0)  {humidite = 0;}
  if(humidite > 99) {humidite = 99;}
  // Valeurs
  chaine = negatif*10000 + absdegres*100 + humidite;
  // Conversion du int en tableau de chars 
  itoa(chaine,Message,10);  // 10 car décimal
  // Séquence de transmission
  digitalWrite(led, HIGH);
  vw_send((uint8_t *)Message, strlen(Message));
  vw_wait_tx(); // On attend la fin de la transmission
  digitalWrite(led, LOW);
  delay(2000);  // et on se repose un peu...
}
